# Fritzing sketch Fan_Wiring_Diagram (saved by Fritzing 1.0.7)
breadboards: 1

parts:
  esp2 = ESP32 DevKitc V4
  A2 = DHT22 module
  OLED2 = SSD1306 0,96" OLED 128x64 I2C
  F2 = Fan - Ventilador [package=THT]
  Q2 = MOSFET-NCHANNEL [package=to220v]
  R3 = Resistor [tolerance=±5% resistance=220 package="1206 [SMD]"]
  D2 = Diode [package=diode-1n4148]
  R4 = Resistor [tolerance=±5% resistance=220 package="0402 [SMD]"]

nets:
  N1: esp2.IO4, A2.Out
  N2: esp2.IO18, R3.Pin_1
  N3: esp2.IO21, OLED2.SDA
  N4: esp2.IO22, OLED2.SCK
  GND: esp2.GND, A2.-, OLED2.GND, Q2.S, R4.Pin_0
  3V3: esp2.3V3, A2.+, OLED2.VDD
  N5: F2.5V, D2.C
  N6: F2.GND, Q2.D, D2.A
  N7: Q2.G, R3.Pin_0, R4.Pin_1

custom parts:
  ESP32 DevKitc V4: ESP32-DevKitC board with ESP32-WROOM-32 module. ESP32-DevKitC V4 is a small-sized ESP32-based development board produced by Espressif. Most of the pins on the ESP module are broken out to the pin headers on the board. The pins D0, D1, D2, D3, CMD and CLK are used internally for communication between ESP32 and SPI flash memory. They are grouped on both sides near the USB connector. Avoid using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
  DHT22 module: DHT22 module. Pins VCC Data GND.
  SSD1306 0,96" OLED 128x64 I2C: YUS
  Fan - Ventilador: Ventilador de 2 pines, se encuentra comunmente en computadoras de escritorio
